// Logisim project s-mips.circ as structural Verilog: 24 circuits, main circuit S-MIPS Board
module S_MIPS_Board (
  input  DESHABILITAR_DISPATCHER,
  output halt
);

  wire button_1_out, CLK, CS, d_ff_1_q, LCLR, LoadRAM, LoadRAMOn, LW, R_R_W, R_W, ram_dispatcher_1_finished,
       RCS, Reset_out, RST, TTY_EN;
  wire [2:0] KDB;
  wire [3:0] LMask, Mask, ram_1_read_time, ram_1_write_time, RMask;
  wire [6:0] KDB_DATA, TTY_DATA;
  wire [15:0] Addr, LAddr, RAddr;
  wire [31:0] I0, I1, I2, I3, LData, ram_1_data_out_0, ram_1_data_out_1, ram_1_data_out_2, ram_1_data_out_3,
       RI0, RI1, RI2, RI3;

  TTY #(.rows(25), .cols(80)) tty_1 (.data(TTY_DATA), .clk(CLK), .we(TTY_EN), .clr(RST));
  not not_1 (LoadRAMOn, ram_dispatcher_1_finished);
  RAM_Dispatcher ram_dispatcher_1 (
    .WriteTime(ram_1_write_time), .Clock(CLK), .Data(LData), .Address(LAddr), .Mask(LMask),
    .Finished(ram_dispatcher_1_finished), .Write(LW), .CLR(LCLR));
  Keyboard #(.buflen(64)) keyboard_1 (.clk(CLK), .re(KDB[0]), .avail(KDB[2]), .data(KDB_DATA));  // open: clr
  RAM ram_1 (
    .Address(RAddr), .Data_Out_0(ram_1_data_out_0), .Data_Out_1(ram_1_data_out_1),
    .Data_Out_2(ram_1_data_out_2), .Data_Out_3(ram_1_data_out_3), .Data_In_0(RI0), .Data_In_1(RI1),
    .Data_In_2(RI2), .Data_In_3(RI3), .Mask(RMask), .nRead_Write(R_R_W), .Chip_Select(RCS),
    .Read_Time(ram_1_read_time), .Reset(button_1_out), .Write_Time(ram_1_write_time));
  Button button_1 (.out(button_1_out));
  D_Flip_Flop d_ff_1 (.clk(CLK), .D(1'b1), .Q(d_ff_1_q), .reset(Reset_out));  // open: Qn, preset, en
  Button Reset (.out(Reset_out));
  S_MIPS s_mips_1 (
    .Kbd_Enable(KDB[0]), .Address(Addr), .Kbd_Clear(KDB[1]), .Kbd_Available(KDB[2]), .RAM_In_0(I0),
    .Kbd_ASCII_Data(KDB_DATA), .RAM_In_1(I1), .TTY_Enable(TTY_EN), .RAM_In_2(I2), .RAM_In_3(I2),
    .TTY_ASCII_Data(TTY_DATA), .Reset(RST), .RAM_Out_0(ram_1_data_out_0), .Clock(CLK),
    .RAM_Out_1(ram_1_data_out_1), .Stop(halt), .RAM_Out_2(ram_1_data_out_2), .RAM_Out_3(ram_1_data_out_3),
    .Mask(Mask), .Read_Time(ram_1_read_time), .Write_Time(ram_1_write_time), .nRead_Write(R_W),
    .Chip_Select(CS));
  D_Flip_Flop d_ff_2 (.clk(CLK), .D(d_ff_1_q), .Qn(LCLR), .reset(Reset_out));  // open: Q, preset, en
  or or_1 (RST, LCLR, LoadRAM);
  Clock clock_1 (.out(CLK));
  Multiplexer #(.width(32), .enable("false")) multiplexer_1 (.in0(I0), .in1(LData), .out(RI0), .sel(LoadRAM));
  Multiplexer #(.width(32), .enable("false")) multiplexer_2 (.in0(I1), .in1(LData), .out(RI1), .sel(LoadRAM));
  Multiplexer #(.width(32), .enable("false")) multiplexer_3 (.in0(I2), .in1(LData), .out(RI2), .sel(LoadRAM));
  Multiplexer #(.width(32), .enable("false")) multiplexer_4 (.in0(I3), .in1(LData), .out(RI3), .sel(LoadRAM));
  and and_1 (LoadRAM, ~DESHABILITAR_DISPATCHER, LoadRAMOn);  // AND_Gate
  Multiplexer #(.width(16), .enable("false")) multiplexer_5 (.in0(Addr), .in1(LAddr), .out(RAddr), .sel(LoadRAM));
  Multiplexer #(.width(4), .enable("false")) multiplexer_6 (.in0(Mask), .in1(LMask), .out(RMask), .sel(LoadRAM));
  Multiplexer #(.enable("false")) multiplexer_7 (.in0(CS), .in1(LW), .out(RCS), .sel(LoadRAM));
  Multiplexer #(.enable("false")) multiplexer_8 (.in0(R_W), .in1(LW), .out(R_R_W), .sel(LoadRAM));

  // Notes on the sheet:
  //   NO MODIFICAR
  //   Keyboard
endmodule

module RAM (
  input  [15:0] Address,
  input  [31:0] Data_In_0,
  input  [31:0] Data_In_1,
  input  [31:0] Data_In_2,
  input  [31:0] Data_In_3,
  input  [3:0] Mask,
  input  nRead_Write,
  input  Chip_Select,
  input  Reset,
  output [31:0] Data_Out_0,
  output [31:0] Data_Out_1,
  output [31:0] Data_Out_2,
  output [31:0] Data_Out_3,
  output [3:0] Read_Time,
  output [3:0] Write_Time
);

  wire and_2_out, and_3_out, and_4_out, and_5_out, and_6_out, and_7_out, and_8_out, and_9_out, Changed, CLK,
       comparator_2_eq, comparator_3_eq, comparator_4_eq, comparator_5_eq, comparator_6_eq, Count,
       demultiplexer_3_out0, Idle, Idle_q, Load, Load0, Load1, nand_1_out, or_1_out, or_2_out, or_3_out,
       or_4_out, or_5_out, or_6_out, or_7_out, or_8_out, or_9_out, or_10_out, Proc_q, Update_Mem, Zero_Time;
  wire [3:0] counter_1_q, multiplexer_1_out, subtractor_1_out;
  wire [31:0] register_1_q, register_2_q, register_3_q, register_4_q, register_5_q;

  // Probe on 4'b0011
  // Probe on 4'b0010
  Multiplexer #(.width(4), .enable("false")) multiplexer_1 (
    .in0(4'b0011), .in1(4'b0010), .out(multiplexer_1_out), .sel(nRead_Write));
  or or_1 (or_1_out, Idle, Update_Mem);
  or or_2 (or_2_out, ~Chip_Select, Reset);  // OR_Gate
  Subtractor #(.width(4)) subtractor_1 (.a(multiplexer_1_out), .b(4'b0010), .out(subtractor_1_out));  // open: bin, bout
  D_Flip_Flop u_Idle (.clk(CLK), .D(or_1_out), .Q(Idle_q), .preset(or_2_out));  // open: Qn, en, reset
  Demultiplexer #(.enable("false")) demultiplexer_1 (.out0(Idle), .out1(Load0), .in(Idle_q), .sel(Changed));
  // Probe on counter_1_q
  Counter #(.width(4), .max('hf)) counter_1 (
    .load(Load), .D(subtractor_1_out), .count(Count), .Q(counter_1_q), .clk(CLK), .clr(or_3_out));  // open: carry
  or or_3 (or_3_out, ~Chip_Select, Reset);  // OR_Gate
  Comparator_part #(.width(4), .mode("unsigned")) comparator_1 (
    .a(4'b0000), .b(counter_1_q), .eq(Zero_Time));  // open: gt, lt
  or or_4 (or_4_out, Count, Load0, Load1);
  Register #(.width(32)) register_1 (.D(Data_In_0), .en(Chip_Select), .Q(register_1_q), .clk(CLK), .clr(or_5_out));
  or or_5 (or_5_out, ~Chip_Select, Reset);  // OR_Gate
  Register #(.width(32)) register_2 (.D(Data_In_1), .en(Chip_Select), .Q(register_2_q), .clk(CLK), .clr(or_6_out));
  or or_6 (or_6_out, ~Chip_Select, Reset);  // OR_Gate
  Register #(.width(32)) register_3 (.D(Data_In_2), .en(Chip_Select), .Q(register_3_q), .clk(CLK), .clr(or_7_out));
  or or_7 (or_7_out, ~Chip_Select, Reset);  // OR_Gate
  Register #(.width(32)) register_4 (.D(Data_In_3), .en(Chip_Select), .Q(register_4_q), .clk(CLK), .clr(or_8_out));
  or or_8 (or_8_out, ~Chip_Select, Reset);  // OR_Gate
  Register #(.width(32)) register_5 (
    .D({{11{1'b1}}, nRead_Write, Mask, Address}), .en(Chip_Select), .Q(register_5_q), .clk(CLK),
    .clr(or_9_out));
  or or_9 (or_9_out, ~Chip_Select, Reset);  // OR_Gate
  D_Flip_Flop Proc (.clk(CLK), .D(or_4_out), .Q(Proc_q), .reset(or_10_out));  // open: Qn, preset, en
  or or_10 (or_10_out, ~Chip_Select, Reset);  // OR_Gate
  Demultiplexer #(.enable("false")) demultiplexer_2 (
    .out0(Count), .out1(Update_Mem), .in(demultiplexer_3_out0), .sel(Zero_Time));
  Demultiplexer #(.enable("false")) demultiplexer_3 (
    .out0(demultiplexer_3_out0), .out1(Load1), .in(Proc_q), .sel(Changed));
  Clock clock_1 (.out(CLK));
  Comparator_part #(.width(32)) comparator_2 (.a(register_1_q), .b(Data_In_0), .eq(comparator_2_eq));  // open: gt, lt
  Comparator_part #(.width(32)) comparator_3 (.a(register_2_q), .b(Data_In_1), .eq(comparator_3_eq));  // open: gt, lt
  Comparator_part #(.width(32)) comparator_4 (.a(register_3_q), .b(Data_In_2), .eq(comparator_4_eq));  // open: gt, lt
  Comparator_part #(.width(32)) comparator_5 (.a(register_4_q), .b(Data_In_3), .eq(comparator_5_eq));  // open: gt, lt
  Comparator_part #(.width(32)) comparator_6 (
    .a(register_5_q), .b({{11{1'b1}}, nRead_Write, Mask, Address}), .eq(comparator_6_eq));  // open: gt, lt
  nand nand_1 (nand_1_out, comparator_6_eq, comparator_2_eq, comparator_3_eq, comparator_4_eq, comparator_5_eq);
  and and_1 (Changed, nand_1_out, Chip_Select);
  or or_11 (Load, Count, Load1, Load0);
  and and_2 (and_2_out, Mask[0], Update_Mem, nRead_Write);
  and and_3 (and_3_out, Mask[1], Update_Mem, nRead_Write);
  and and_4 (and_4_out, Mask[2], Update_Mem, nRead_Write);
  and and_5 (and_5_out, Mask[3], Update_Mem, nRead_Write);
  RAM_part #(.addrWidth(16), .dataWidth(32), .bus("separate")) ram_1 (
    .addr(Address), .din(Data_In_0), .data(Data_Out_0), .str(and_2_out), .sel(Chip_Select), .clk(CLK),
    .ld(and_6_out), .clr(Reset));
  and and_6 (and_6_out, ~nRead_Write, Idle);  // AND_Gate
  RAM_part #(.addrWidth(16), .dataWidth(32), .bus("separate")) ram_2 (
    .addr(Address), .din(Data_In_1), .data(Data_Out_1), .str(and_3_out), .sel(Chip_Select), .clk(CLK),
    .ld(and_7_out), .clr(Reset));
  and and_7 (and_7_out, ~nRead_Write, Idle);  // AND_Gate
  RAM_part #(.addrWidth(16), .dataWidth(32), .bus("separate")) ram_3 (
    .addr(Address), .din(Data_In_2), .data(Data_Out_2), .str(and_4_out), .sel(Chip_Select), .clk(CLK),
    .ld(and_8_out), .clr(Reset));
  and and_8 (and_8_out, ~nRead_Write, Idle);  // AND_Gate
  RAM_part #(.addrWidth(16), .dataWidth(32), .bus("separate")) ram_4 (
    .addr(Address), .din(Data_In_3), .data(Data_Out_3), .str(and_5_out), .sel(Chip_Select), .clk(CLK),
    .ld(and_9_out), .clr(Reset));
  and and_9 (and_9_out, ~nRead_Write, Idle);  // AND_Gate

  assign Read_Time = 4'b0011;
  assign Write_Time = 4'b0010;

  // Other names for the same wires on the sheet: M0 = Mask[0]; M1 = Mask[1]; M2 = Mask[2]; M3 = Mask[3];
  //   RW = nRead_Write; CLR = Reset; CS = Chip_Select; Load2 = Count

  // Notes on the sheet:
  //   NO MODIFICAR
  //   excepto quizás los valores RT y WT
  //   BANK0
  //   BANK1
  //   BANK2
  //   BANK3
endmodule

module S_MIPS (
  input  Kbd_Available,
  input  [6:0] Kbd_ASCII_Data,
  input  [31:0] RAM_Out_0,
  input  [31:0] RAM_Out_1,
  input  Reset,
  input  [31:0] RAM_Out_2,
  input  Clock,
  input  [31:0] RAM_Out_3,
  input  [3:0] Read_Time,
  input  [3:0] Write_Time,
  output Kbd_Enable,
  output [15:0] Address,
  output Kbd_Clear,
  output TTY_Enable,
  output [6:0] TTY_ASCII_Data,
  output Stop,
  output [31:0] RAM_In_0,
  output [31:0] RAM_In_1,
  output [31:0] RAM_In_2,
  output [31:0] RAM_In_3,
  output [3:0] Mask,
  output nRead_Write,
  output Chip_Select
);

  wire Alu_Inst, d_ff_1_q, En_GI, En_Gi_t, En_PC, En_RF, Get_Data, Get_Inst, Halt, Jmp_Inst, Mem_Inst,
       or_1_out, or_2_out, R_Inst, Ready_Data, Ready_Inst, Ready_Write, Stack_Inst, Start, Tty, Write,
       Write_Inst;
  wire [6:0] Tty_Data_t;
  wire [31:0] Address_t, Data_In, data_path_1_r_out, multiplexer_1_out, multiplexer_2_out, multiplexer_3_out,
       multiplexer_4_out, R_out_t, ram_interaction_1_bank_output_1, ram_interaction_1_bank_output_2,
       ram_interaction_1_bank_output_3, ram_interaction_1_bank_output_4, Ram_Output_0_t, Ram_Output_1_t,
       Ram_Output_2_t, Ram_Output_3_t;

  D_Flip_Flop #(.trigger("falling")) d_ff_1 (
    .clk(Clock), .D(Get_Inst), .Q(d_ff_1_q), .en(or_1_out));  // open: Qn, preset, reset
  or or_1 (or_1_out, Get_Inst, Ready_Inst);
  Multiplexer #(.width(32), .enable("false")) multiplexer_1 (
    .in0(Ram_Output_0_t), .in1(RAM_Out_1), .out(multiplexer_1_out), .sel(Write));
  Multiplexer #(.width(32), .enable("false")) multiplexer_2 (
    .in0(Ram_Output_2_t), .in1(RAM_Out_1), .out(multiplexer_2_out), .sel(Write));
  Multiplexer #(.width(32), .enable("false")) multiplexer_3 (
    .in0(Ram_Output_1_t), .in1(RAM_Out_1), .out(multiplexer_3_out), .sel(Write));
  Multiplexer #(.width(32), .enable("false")) multiplexer_4 (
    .in0(Ram_Output_3_t), .in1(RAM_Out_1), .out(multiplexer_4_out), .sel(Write));
  or or_2 (or_2_out, Mem_Inst, Stack_Inst);
  D_Flip_Flop #(.trigger("falling")) d_ff_2 (.clk(Clock), .D(Reset), .Q(Start));  // open: Qn, preset, en, reset
  Ram_Interaction ram_interaction_1 (
    .Clk(Reset), .Reset(Reset), .Bank_1(multiplexer_1_out), .Bank_3(multiplexer_2_out),
    .DP_Address(Address_t), .Write(Write), .Get_Inst(Get_Inst), .Get_Data(Get_Data), .Is_Inst(En_Gi_t),
    .Read_Time(Read_Time), .Bank_2(multiplexer_3_out), .Bank_4(multiplexer_4_out), .Write_Time(Write_Time),
    .ADDR(Address), .Bank_Output_1(ram_interaction_1_bank_output_1),
    .Bank_Output_3(ram_interaction_1_bank_output_3), .Mask(Mask), .RW(nRead_Write), .CS(Chip_Select),
    .Bank_Output_2(ram_interaction_1_bank_output_2), .Bank_Output_4(ram_interaction_1_bank_output_4),
    .Ready_Inst(Ready_Inst), .Ready_Data(Ready_Data), .Ready_Write(Ready_Write));
  Data_Path data_path_1 (
    .Clk(Clock), .Reset(Reset), .Instruction(Data_In), .MemW(d_ff_1_q), .EnGI(En_GI), .EnPC(En_PC),
    .kbd_data(Kbd_ASCII_Data), .EnRF(En_RF), .KbdAva(Kbd_Available), .Alu_Inst(Alu_Inst), .Halt(Halt),
    .R_out(data_path_1_r_out), .Tty(Tty), .Mem_Inst(Mem_Inst), .Stack_Inst(Stack_Inst), .Jmp_Inst(Jmp_Inst),
    .Write_Inst(Write_Inst), .Tty_Data(Tty_Data_t), .R_Inst(R_Inst), .Address(Address_t));
  Multiplexer #(.select(2), .width(32), .enable("false")) multiplexer_5 (
    .in0(ram_interaction_1_bank_output_1), .in1(ram_interaction_1_bank_output_2),
    .in2(ram_interaction_1_bank_output_3), .in3(ram_interaction_1_bank_output_4), .out(Data_In),
    .sel(Address_t[3:2]));
  InOut inout_1 (.in_1(data_path_1_r_out), .Output(R_out_t));
  Control_Unit control_unit_1 (
    .Clk(Clock), .Start(Start), .Ready_Inst(Ready_Inst), .Alu_Inst(Alu_Inst), .R_Inst(R_Inst), .Reset(Reset),
    .Tty_Inst(Tty), .Ready_Data(Ready_Data), .Jmp_Inst(Jmp_Inst), .Mem_Inst(or_2_out),
    .Write_Inst(Write_Inst), .Ready_W(Ready_Write), .Use_RF(En_RF), .End(Stop), .Get_Inst(Get_Inst),
    .Tty_En(TTY_Enable), .Write(Write), .Use_PC(En_PC), .Get_Data(Get_Data), .Use_GI(En_Gi_t),
    .Kbd_En(Kbd_Enable));

  assign Kbd_Clear = Reset;
  assign RAM_Out_2 = RAM_Out_1;
  assign RAM_Out_3 = RAM_Out_1;

  // Other names for the same wires on the sheet: CLK = Clock; CS = Chip_Select; KBD_AVAIL = Kbd_Available;
  //   CLR = Reset; KBD_CLR = Reset; KBD_DATA[6:0] = Kbd_ASCII_Data; RAM_A[15:0] = Address;
  //   RAM_INPUT_0[31:0] = RAM_In_0; RAM_INPUT_1[31:0] = RAM_In_1; RAM_INPUT_2[31:0] = RAM_In_2;
  //   RAM_INPUT_3[31:0] = RAM_In_3; RAM_MASK[3:0] = Mask; RAM_OUTPUT_0[31:0] = RAM_Out_0; R_Out[31:0] = RAM_Out_1;
  //   RAM_OUTPUT_1[31:0] = RAM_Out_1; RAM_OUTPUT_2[31:0] = RAM_Out_1; RAM_OUTPUT_3[31:0] = RAM_Out_1;
  //   RAM_OUTPUT_4[31:0] = RAM_Out_1; RW = nRead_Write; TTY_DATA[6:0] = TTY_ASCII_Data

  // Notes on the sheet:
  //   RAM ADDRESS
  //   DATA FROM RAM
  //   DATA TO RAM
  //   DATA WRITE MASK
  //   RAM TIMING
  //   RAM CONTROL
  //   KEYBOARD
  //   TTY
  //   SEQUENCING
endmodule

module RAM_Dispatcher (
  input  [3:0] WriteTime,
  input  Clock,
  input  CLR,
  output [31:0] Data,
  output [15:0] Address,
  output [3:0] Mask,
  output Finished,
  output Write
);

  wire demultiplexer_2_out1, demultiplexer_3_out1, End, IDLE_q, IncAddr, Load, or_1_out, or_2_out, While_q,
       WriteEnd;
  wire [3:0] counter_1_q;
  wire [31:0] CurrentAddress_q;

  Counter #(.width(32), .max('hffffffff)) CurrentAddress (
    .count(IncAddr), .Q({CurrentAddress_q[31:18], Address, CurrentAddress_q[1:0]}), .clk(Clock), .clr(CLR));  // open: load, D, carry
  or or_1 (or_1_out, IncAddr, demultiplexer_3_out1, Finished);
  D_Flip_Flop IDLE (.clk(Clock), .D(or_1_out), .Q(IDLE_q), .preset(CLR));  // open: Qn, en, reset
  Demultiplexer #(.enable("false")) demultiplexer_1 (.out0(Load), .out1(Finished), .in(IDLE_q), .sel(End));
  D_Flip_Flop While (.clk(Clock), .D(or_2_out), .Q(While_q), .reset(CLR));  // open: Qn, preset, en
  or or_2 (or_2_out, Write, Load);
  RAM_part #(.addrWidth(18), .dataWidth(32)) ram_1 (
    .addr({Address, CurrentAddress_q[1:0]}), .data(Data), .clk(Clock));  // open: sel, ld, clr
  Demultiplexer #(.enable("false")) demultiplexer_2 (
    .out0(Write), .out1(demultiplexer_2_out1), .in(While_q), .sel(WriteEnd));
  Decoder #(.select(2)) decoder_1 (
    .out0(Mask[0]), .out1(Mask[1]), .out2(Mask[2]), .out3(Mask[3]), .sel(CurrentAddress_q[1:0]));  // open: en
  Demultiplexer #(.enable("false")) demultiplexer_3 (
    .out0(IncAddr), .out1(demultiplexer_3_out1), .in(demultiplexer_2_out1), .sel(End));
  Counter #(.width(4), .max('hf)) counter_1 (
    .load(Load), .D(WriteTime), .count(Write), .Q(counter_1_q), .clk(Clock));  // open: carry, clr
  Comparator_part #(.width(32)) comparator_1 (.a(Data), .b({32{1'b1}}), .eq(End));  // open: gt, lt
  Comparator_part #(.width(4)) comparator_2 (.a(4'b0000), .b(counter_1_q), .eq(WriteEnd));  // open: gt, lt

  // Other names for the same wires on the sheet: CLK = Clock; Count = Write; WT[3:0] = WriteTime
endmodule

module Comparator (
  input  [31:0] A,
  input  [31:0] B,
  input  Unsigned,
  output [31:0] A_B
);

  wire comparator_1_lt;

  Comparator_part #(.width(32)) comparator_1 (.a(A), .b(B), .lt(comparator_1_lt));  // open: gt, eq
  assign A_B = {{31{1'b0}}, comparator_1_lt};  // Bit_Extender bit_extender_1
endmodule

module Timer (
  input  Start,
  input  Reset,
  input  Clk,
  input  [3:0] Time,
  output Ready
);

  wire [3:0] counter_1_q;

  Counter #(.width(4), .max('hf)) counter_1 (
    .count(Start), .Q(counter_1_q), .clk(Clk), .clr(Reset));  // open: load, D, carry
  Comparator_part #(.width(4)) comparator_1 (.a(Time), .b(counter_1_q), .eq(Ready));  // open: gt, lt
endmodule

module PC (
  input  [31:0] Input,
  input  Enable,
  input  Reset,
  input  Clk,
  output [31:0] Output
);

  Register #(.width(32)) register_1 (.D(Input), .en(Enable), .Q(Output), .clk(Clk), .clr(Reset));
endmodule

module Register_File (
  input  Reset,
  input  Write,
  input  [4:0] IN_A,
  input  [31:0] Input,
  input  Pop,
  input  [4:0] IN_B,
  input  MemRW,
  input  Clk,
  input  Push,
  input  [4:0] SEL,
  output [31:0] Output_A,
  output [31:0] Output_B,
  output [31:0] Output_SP
);

  wire In31, L0, L1, L2, L3, L4, L5, L6, L7, L8, L9, L10, L11, L12, L13, L14, L15, L16, L17, L18, L19, L20,
       L21, L22, L23, L24, L25, L26, L27, L28, L29, L30, L31, or_1_out;
  wire [31:0] adder_1_out, multiplexer_1_out, multiplexer_2_out, multiplexer_3_out, Out0, Out1, Out2, Out3,
       Out4, Out5, Out6, Out7, Out8, Out9, Out10, Out11, Out12, Out13, Out14, Out15, Out16, Out17, Out18,
       Out19, Out20, Out21, Out22, Out23, Out24, Out25, Out26, Out27, Out28, Out29, Out30, subtractor_1_out;

  Register #(.width(32)) register_1 (.D(Input), .en(L21), .Q(Out21), .clk(Clk), .clr(Reset));
  Register #(.width(32)) register_2 (.D(Input), .en(L24), .Q(Out24), .clk(Clk), .clr(Reset));
  Register #(.width(32)) register_3 (.D({32{1'b0}}), .en(L0), .Q(Out0), .clk(Clk), .clr(Reset));
  Register #(.width(32)) register_4 (.D(Input), .en(L3), .Q(Out3), .clk(Clk), .clr(Reset));
  Register #(.width(32)) register_5 (.D(Input), .en(L6), .Q(Out6), .clk(Clk), .clr(Reset));
  Register #(.width(32)) register_6 (.D(Input), .en(L9), .Q(Out9), .clk(Clk), .clr(Reset));
  Register #(.width(32)) register_7 (.D(Input), .en(L12), .Q(Out12), .clk(Clk), .clr(Reset));
  Register #(.width(32)) register_8 (.D(Input), .en(L15), .Q(Out15), .clk(Clk), .clr(Reset));
  Register #(.width(32)) register_9 (.D(Input), .en(L18), .Q(Out18), .clk(Clk), .clr(Reset));
  Register #(.width(32)) register_10 (.D(Input), .en(L27), .Q(Out27), .clk(Clk), .clr(Reset));
  Register #(.width(32)) register_11 (.D(Input), .en(L30), .Q(Out30), .clk(Clk), .clr(Reset));
  Register #(.width(32)) register_12 (.D(Input), .en(L10), .Q(Out10), .clk(Clk), .clr(Reset));
  Register #(.width(32)) register_13 (.D(Input), .en(L13), .Q(Out13), .clk(Clk), .clr(Reset));
  Register #(.width(32)) register_14 (.D(Input), .en(L16), .Q(Out16), .clk(Clk), .clr(Reset));
  Register #(.width(32)) register_15 (.D(Input), .en(L19), .Q(Out19), .clk(Clk), .clr(Reset));
  Register #(.width(32)) register_16 (.D(Input), .en(L22), .Q(Out22), .clk(Clk), .clr(Reset));
  Register #(.width(32)) register_17 (.D(Input), .en(L25), .Q(Out25), .clk(Clk), .clr(Reset));
  Register #(.width(32)) register_18 (.D(Input), .en(L28), .Q(Out28), .clk(Clk), .clr(Reset));
  Register #(.width(32)) register_19 (.D(Input), .en(L1), .Q(Out1), .clk(Clk), .clr(Reset));
  Register #(.width(32)) register_20 (.D(Input), .en(L4), .Q(Out4), .clk(Clk), .clr(Reset));
  Register #(.width(32)) register_21 (.D(Input), .en(L7), .Q(Out7), .clk(Clk), .clr(Reset));
  Register #(.width(32)) register_22 (.D(Input), .en(L23), .Q(Out23), .clk(Clk), .clr(Reset));
  Register #(.width(32)) register_23 (.D(Input), .en(L26), .Q(Out26), .clk(Clk), .clr(Reset));
  Register #(.width(32)) register_24 (.D(Input), .en(L2), .Q(Out2), .clk(Clk), .clr(Reset));
  Register #(.width(32)) register_25 (.D(Input), .en(L5), .Q(Out5), .clk(Clk), .clr(Reset));
  Register #(.width(32)) register_26 (.D(Input), .en(L8), .Q(Out8), .clk(Clk), .clr(Reset));
  Register #(.width(32)) register_27 (.D(Input), .en(L11), .Q(Out11), .clk(Clk), .clr(Reset));
  Register #(.width(32)) register_28 (.D(Input), .en(L14), .Q(Out14), .clk(Clk), .clr(Reset));
  Register #(.width(32)) register_29 (.D(Input), .en(L17), .Q(Out17), .clk(Clk), .clr(Reset));
  Register #(.width(32)) register_30 (.D(Input), .en(L20), .Q(Out20), .clk(Clk), .clr(Reset));
  Register #(.width(32)) register_31 (.D(Input), .en(L29), .Q(Out29), .clk(Clk), .clr(Reset));
  or or_1 (or_1_out, Push, Pop);
  Demultiplexer #(.select(5), .enable("false")) demultiplexer_1 (
    .out0(L0), .out1(L1), .out2(L2), .out3(L3), .out4(L4), .out5(L5), .out6(L6), .out7(L7), .out8(L8),
    .out9(L9), .out10(L10), .out11(L11), .out12(L12), .out13(L13), .out14(L14), .out15(L15), .out16(L16),
    .out17(L17), .out18(L18), .out19(L19), .out20(L20), .out21(L21), .out22(L22), .out23(L23), .out24(L24),
    .out25(L25), .out26(L26), .out27(L27), .out28(L28), .out29(L29), .out30(L30), .out31(In31), .in(Write),
    .sel(SEL));
  Demultiplexer #(.select(5), .width(32)) demultiplexer_2 (
    .out0(Out0), .out1(Out1), .out2(Out2), .out3(Out3), .out4(Out4), .out5(Out5), .out6(Out6), .out7(Out7),
    .out8(Out8), .out9(Out9), .out10(Out10), .out11(Out11), .out12(Out12), .out13(Out13), .out14(Out14),
    .out15(Out15), .out16(Out16), .out17(Out17), .out18(Out18), .out19(Out19), .out20(Out20), .out21(Out21),
    .out22(Out22), .out23(Out23), .out24(Out24), .out25(Out25), .out26(Out26), .out27(Out27), .out28(Out28),
    .out29(Out29), .out30(Out30), .out31(Output_SP), .in(Output_A), .sel(IN_A));  // open: en
  Demultiplexer #(.select(5), .width(32)) demultiplexer_3 (
    .out0(Out0), .out1(Out1), .out2(Out2), .out3(Out3), .out4(Out4), .out5(Out5), .out6(Out6), .out7(Out7),
    .out8(Out8), .out9(Out9), .out10(Out10), .out11(Out11), .out12(Out12), .out13(Out13), .out14(Out14),
    .out15(Out15), .out16(Out16), .out17(Out17), .out18(Out18), .out19(Out19), .out20(Out20), .out21(Out21),
    .out22(Out22), .out23(Out23), .out24(Out24), .out25(Out25), .out26(Out26), .out27(Out27), .out28(Out28),
    .out29(Out29), .out30(Out30), .out31(Output_SP), .in(Output_B), .sel(IN_B));  // open: en
  and and_1 (L31, MemRW, or_1_out);
  Subtractor #(.width(32)) subtractor_1 (.a(Output_SP), .b(32'h4), .out(subtractor_1_out));  // open: bin, bout
  Multiplexer #(.width(32), .enable("false")) multiplexer_1 (
    .in0(subtractor_1_out), .in1(adder_1_out), .out(multiplexer_1_out), .sel(Pop));
  Adder #(.width(32)) adder_1 (.a(Output_SP), .b(32'h4), .out(adder_1_out));  // open: cin, cout
  Multiplexer #(.width(32), .enable("false")) multiplexer_2 (
    .in0(multiplexer_1_out), .in1({32{1'b0}}), .out(multiplexer_2_out), .sel(Reset));
  Multiplexer #(.width(32), .enable("false")) multiplexer_3 (
    .in0(Input), .in1(multiplexer_2_out), .out(multiplexer_3_out), .sel(In31));
  Register #(.width(32)) register_32 (.D(multiplexer_3_out), .en(Clk), .Q(Output_SP), .clk(Clk));  // open: clr
  or or_2 (Clk, In31, L31, Reset);

  // Other names for the same wires on the sheet: A[31:0] = Output_A; B[31:0] = Output_B; Out31[31:0] = Output_SP;
  //   OutA[4:0] = IN_A; OutB[4:0] = IN_B
endmodule

module Abs (
  input  [31:0] in_1,
  input  Unsigned,
  output [31:0] Value,
  output Sig
);

  wire and_1_out;
  wire [31:0] negator_1_out;

  Negator #(.width(32)) negator_1 (.in(in_1), .out(negator_1_out));
  and and_1 (and_1_out, in_1[31], ~Unsigned);  // AND_Gate
  Multiplexer #(.width(32), .enable("false")) multiplexer_1 (
    .in0(in_1), .in1(negator_1_out), .out(Value), .sel(and_1_out));

  assign Sig = in_1[31];
endmodule

module Multiplier (
  input  [31:0] in_1,
  input  [31:0] in_2,
  input  in_3,
  output [31:0] FHI,
  output [31:0] FLO
);

  wire adder_1_cout, SEL, SigA, SigB, SignA, xor_1_out;
  wire [31:0] AbsA, AbsB, bit_extender_1_out, HI, LO, not_1_out, not_2_out, SHI, SLO;

  Abs abs_1 (.in_1(in_1), .Sig(SigA), .Value(AbsA), .Unsigned(in_3));
  Abs abs_2 (.in_1(in_2), .Sig(SigB), .Value(AbsB), .Unsigned(in_3));
  xor xor_1 (xor_1_out, SigA, SigB);
  Multiplier_part #(.width(32)) multiplier_1 (.a(AbsA), .b(AbsB), .out(LO), .cout(HI));  // open: cin
  and and_1 (SEL, xor_1_out, ~SignA);  // AND_Gate
  Multiplexer #(.width(32), .enable("false")) multiplexer_1 (.in0(LO), .in1(SLO), .out(FLO), .sel(SEL));
  Multiplexer #(.width(32), .enable("false")) multiplexer_2 (.in0(HI), .in1(SHI), .out(FHI), .sel(SEL));
  assign not_1_out = ~LO;  // NOT_Gate not_1, 32 bits wide
  Adder #(.width(32)) adder_1 (.a(not_1_out), .b(32'h1), .out(SLO), .cout(adder_1_cout));  // open: cin
  assign bit_extender_1_out = {{31{1'b0}}, adder_1_cout};  // Bit_Extender bit_extender_1
  assign not_2_out = ~HI;  // NOT_Gate not_2, 32 bits wide
  Adder #(.width(32)) adder_2 (.a(not_2_out), .b(bit_extender_1_out), .out(SHI));  // open: cin, cout

  // Other names for the same wires on the sheet: A[31:0] = in_1; B[31:0] = in_2; Unsigned = in_3
endmodule

module Divider (
  input  [31:0] in_1,
  input  [31:0] in_2,
  input  in_3,
  output [31:0] A_B,
  output [31:0] R
);

  wire SigA, SigB, xor_1_out;
  wire [31:0] AbsA, AbsB, adder_1_out, divider_1_out, multiplexer_2_out, negator_1_out, R_t, subtractor_1_out;

  Abs abs_1 (.in_1(in_1), .Sig(SigA), .Value(AbsA), .Unsigned(in_3));
  Abs abs_2 (.in_1(in_2), .Sig(SigB), .Value(AbsB), .Unsigned(in_3));
  Multiplexer #(.width(32), .enable("false")) multiplexer_1 (.in0(R_t), .in1(subtractor_1_out), .out(R), .sel(SigA));
  Subtractor #(.width(32)) subtractor_1 (.a(AbsB), .b(R_t), .out(subtractor_1_out));  // open: bin, bout
  Divider_part #(.width(32)) divider_1 (.a(AbsA), .b(AbsB), .out(divider_1_out), .rem(R_t));  // open: upper
  Multiplexer #(.width(32), .enable("false")) multiplexer_2 (
    .in0(divider_1_out), .in1(adder_1_out), .out(multiplexer_2_out), .sel(SigA));
  Adder #(.width(32)) adder_1 (.a(divider_1_out), .b(32'h1), .out(adder_1_out));  // open: cin, cout
  Negator #(.width(32)) negator_1 (.in(multiplexer_2_out), .out(negator_1_out));
  Multiplexer #(.width(32), .enable("false")) multiplexer_3 (
    .in0(multiplexer_2_out), .in1(negator_1_out), .out(A_B), .sel(xor_1_out));
  xor xor_1 (xor_1_out, SigB, SigA);

  // Other names for the same wires on the sheet: A[31:0] = in_1; B[31:0] = in_2; Unsigned = in_3
endmodule

module ALU (
  input  [31:0] A,
  input  [3:0] Select,
  input  On,
  input  Clk,
  input  [31:0] A_2,
  input  Unsigned,
  output [31:0] LO,
  output [31:0] Output_Primaria,
  output [31:0] HI
);

  wire comparator_2_eq, Div, Enable, or_2_out;
  wire [31:0] Add, And, DivC, MulH, MulL, multiplexer_2_out, multiplexer_3_out, Nor, Or, Rest, Slt, Sub, Xor;

  assign And = A & A_2;  // AND_Gate and_1, 32 bits wide
  assign Or = A | A_2;  // OR_Gate or_1, 32 bits wide
  assign Xor = A ^ A_2;  // XOR_Gate xor_1, 32 bits wide
  assign Nor = ~Or;  // NOT_Gate not_1, 32 bits wide
  Comparator comparator_1 (.A(A), .B(A_2), .Unsigned(Unsigned), .A_B(Slt));
  Adder #(.width(32)) adder_1 (.a(A), .b(A_2), .out(Add));  // open: cin, cout
  Subtractor #(.width(32)) subtractor_1 (.a(A), .b(A_2), .out(Sub));  // open: bin, bout
  Multiplier multiplier_1 (.in_1(A), .in_2(A_2), .in_3(Unsigned), .FHI(MulH), .FLO(MulL));
  Divider divider_1 (.in_1(A), .in_2(A_2), .in_3(Unsigned), .A_B(DivC), .R(Rest));
  Multiplexer #(.select(4), .width(32), .enable("false")) multiplexer_1 (
    .in0(Add), .in1(Sub), .in2(And), .in3(Or), .in4(Nor), .in5(Xor), .in6(Slt), .out(Output_Primaria),
    .sel(Select));  // open: in7, in8, in9, in10, in11, in12, in13, in14, in15
  Multiplexer #(.width(32), .enable("false")) multiplexer_2 (
    .in0(MulH), .in1(DivC), .out(multiplexer_2_out), .sel(Div));
  Comparator_part #(.width(4)) comparator_2 (.a(Select), .b(4'b0000), .eq(comparator_2_eq));  // open: gt, lt
  Comparator_part #(.width(4)) comparator_3 (.a(Select), .b(4'b1111), .eq(Div));  // open: gt, lt
  Register #(.width(32)) register_1 (.D(multiplexer_2_out), .en(Enable), .Q(HI), .clk(Clk));  // open: clr
  or or_2 (or_2_out, comparator_2_eq, Div);
  and and_2 (Enable, or_2_out, On);
  Multiplexer #(.width(32), .enable("false")) multiplexer_3 (
    .in0(MulL), .in1(Rest), .out(multiplexer_3_out), .sel(Div));
  Register #(.width(32)) register_2 (.D(multiplexer_3_out), .en(Enable), .Q(LO), .clk(Clk));  // open: clr

  // Other names for the same wires on the sheet: B[31:0] = A_2; OpSelect[3:0] = Select

  // Notes on the sheet:
  //   Logica
  //   Aritmetica
  //   Output Secundaria
endmodule

module Get_Instruction (
  input  [31:0] Instruction,
  input  Enable,
  input  Clk,
  input  Reset,
  output [31:0] Output
);

  Register #(.width(32)) register_1 (
    .D(Instruction), .en(Enable), .Q({Output[7:0], Output[15:8], Output[23:16], Output[31:24]}), .clk(Clk),
    .clr(Reset));
endmodule

module InOut (
  input  [31:0] in_1,
  output [31:0] Output
);


  assign Output = {in_1[7:0], in_1[15:8], in_1[23:16], in_1[31:24]};
endmodule

module Alu_Encoder (
  input  Add,
  input  Sub,
  input  Mult,
  input  Mulu,
  input  Div,
  input  Divu,
  input  Slt,
  input  Sltu,
  input  And,
  input  Or,
  input  Nor,
  input  Xor,
  input  Addi,
  input  Slti,
  input  Sltiu,
  input  Andi,
  input  Xori,
  input  Ori,
  output Output,
  output [3:0] OpSelect,
  output Unsigned,
  output Inmediately
);

  wire ADD_t, AND_t, MUL, OR_t, SLT_t, XOR_t;

  or or_1 (ADD_t, Add, Addi);
  or or_2 (MUL, Mult, Mulu);
  or or_3 (OpSelect[0], ADD_t, OpSelect[3], AND_t, SLT_t, Nor);
  or or_4 (Unsigned, Mulu, Divu, Sltiu, Sltu);
  or or_5 (OpSelect[3], Div, Divu);
  or or_6 (OpSelect[1], Sub, XOR_t, SLT_t, OpSelect[3], AND_t);
  or or_7 (Inmediately, Xori, Slti, Andi, Ori, Sltiu, Addi);
  or or_8 (SLT_t, Slt, Sltu, Sltiu, Slti);
  or or_9 (OpSelect[2], OpSelect[3], OR_t, XOR_t, SLT_t);
  or or_10 (AND_t, And, Andi);
  or or_11 (Output, OpSelect[0], MUL, OR_t, XOR_t);
  or or_12 (OR_t, Or, Ori);
  or or_13 (XOR_t, Xor, Xori);

  // Other names for the same wires on the sheet: _1 = OpSelect[0]; _2 = OpSelect[1]; _3 = OpSelect[2];
  //   DIV_t = OpSelect[3]
endmodule

module TipoI (
  input  [5:0] in_1,
  output Addi,
  output Xori,
  output Beq,
  output Bltz,
  output Slti,
  output Ori,
  output Bne,
  output Sltiu,
  output Lw,
  output Blez,
  output Andi,
  output Sw,
  output Bgtz
);

  wire [5:0] not_1_out, not_2_out, not_3_out, not_4_out, not_5_out, not_6_out, not_7_out, not_8_out,
       not_9_out, not_10_out, not_11_out, not_12_out;

  assign not_1_out = ~in_1;  // NOT_Gate not_1, 6 bits wide
  assign not_2_out = ~in_1;  // NOT_Gate not_2, 6 bits wide
  assign not_3_out = ~in_1;  // NOT_Gate not_3, 6 bits wide
  assign not_4_out = ~in_1;  // NOT_Gate not_4, 6 bits wide
  assign not_5_out = ~in_1;  // NOT_Gate not_5, 6 bits wide
  assign not_6_out = ~in_1;  // NOT_Gate not_6, 6 bits wide
  and and_1 (Addi, not_1_out[0], not_1_out[1], not_1_out[2], ~not_1_out[3], not_1_out[4], not_1_out[5]);  // AND_Gate
  and and_2 (Slti, not_2_out[0], ~not_2_out[1], not_2_out[2], ~not_2_out[3], not_2_out[4], not_2_out[5]);  // AND_Gate
  and and_3 (Sltiu, ~not_3_out[0], ~not_3_out[1], not_3_out[2], ~not_3_out[3], not_3_out[4], not_3_out[5]);  // AND_Gate
  and and_4 (Bne, ~not_4_out[0], not_4_out[1], ~not_4_out[2], not_4_out[3], not_4_out[4], not_4_out[5]);  // AND_Gate
  and and_5 (Blez, not_5_out[0], ~not_5_out[1], ~not_5_out[2], not_5_out[3], not_5_out[4], not_5_out[5]);  // AND_Gate
  and and_6 (Bgtz, ~not_6_out[0], ~not_6_out[1], ~not_6_out[2], not_6_out[3], not_6_out[4], not_6_out[5]);  // AND_Gate
  assign not_7_out = ~in_1;  // NOT_Gate not_7, 6 bits wide
  assign not_8_out = ~in_1;  // NOT_Gate not_8, 6 bits wide
  assign not_9_out = ~in_1;  // NOT_Gate not_9, 6 bits wide
  assign not_10_out = ~in_1;  // NOT_Gate not_10, 6 bits wide
  and and_7 (Andi, not_7_out[0], not_7_out[1], ~not_7_out[2], ~not_7_out[3], not_7_out[4], not_7_out[5]);  // AND_Gate
  and and_8 (Xori, not_8_out[0], ~not_8_out[1], ~not_8_out[2], ~not_8_out[3], not_8_out[4], not_8_out[5]);  // AND_Gate
  and and_9 (Ori, ~not_9_out[0], not_9_out[1], ~not_9_out[2], ~not_9_out[3], not_9_out[4], not_9_out[5]);  // AND_Gate
  and and_10 (Bltz, ~not_10_out[0], not_10_out[1], not_10_out[2], not_10_out[3], not_10_out[4], not_10_out[5]);  // AND_Gate
  assign not_11_out = ~in_1;  // NOT_Gate not_11, 6 bits wide
  assign not_12_out = ~in_1;  // NOT_Gate not_12, 6 bits wide
  and and_11 (Lw, ~not_11_out[0], ~not_11_out[1], not_11_out[2], not_11_out[3], not_11_out[4], ~not_11_out[5]);  // AND_Gate
  and and_12 (Sw, in_1[0], in_1[1], ~in_1[2], in_1[3], ~in_1[4], in_1[5]);  // AND_Gate
  and and_13 (Beq, not_12_out[0], not_12_out[1], ~not_12_out[2], not_12_out[3], not_12_out[4], not_12_out[5]);  // AND_Gate

  // Other names for the same wires on the sheet: Input[5:0] = in_1
endmodule

module Tipo_R (
  input  [5:0] Func_Code,
  input  _000000,
  input  _111000,
  input  _111111,
  output Nop,
  output Mulu,
  output Slt,
  output Nor,
  output Mfhi,
  output Add,
  output Div,
  output Sltu,
  output Xor,
  output Mflo,
  output Sub,
  output Divu,
  output And,
  output Push,
  output Halt,
  output Mul,
  output Pop,
  output Or,
  output Jr,
  output Tty,
  output Rnd,
  output Kbd
);

  wire and_2_out, and_9_out, and_12_out, and_13_out, and_16_out, and_19_out, and_20_out, and_21_out,
       and_23_out, and_24_out, and_25_out, and_26_out, and_35_out, and_36_out, and_37_out, and_38_out, aux,
       nand_1_out, not_2_out;
  wire [5:0] not_1_out;

  assign not_1_out = ~Func_Code;  // NOT_Gate not_1, 6 bits wide
  and and_1 (Mulu, Func_Code[0], aux);
  and and_2 (and_2_out, not_1_out[5], not_1_out[4], not_1_out[3], not_1_out[2], not_1_out[1], not_1_out[0]);
  not not_2 (not_2_out, not_1_out[0]);
  and and_3 (Mul, ~Func_Code[0], aux);  // AND_Gate
  and and_4 (Mfhi, ~Func_Code[1], and_13_out);  // AND_Gate
  and and_5 (Mflo, Func_Code[1], and_13_out);
  and and_6 (Nop, and_2_out, _000000);
  and and_7 (Pop, and_2_out, _111000);
  and and_8 (Push, _111000, not_2_out);
  and and_9 (and_9_out, ~Func_Code[5], Func_Code[4], Func_Code[3], ~Func_Code[2], ~Func_Code[1]);  // AND_Gate
  and and_10 (aux, and_9_out, _000000);
  and and_11 (Nor, Func_Code[5], ~Func_Code[4], ~Func_Code[3], Func_Code[2], Func_Code[1], Func_Code[0], _000000);  // AND_Gate
  and and_12 (and_12_out, ~Func_Code[5], Func_Code[4], ~Func_Code[3], ~Func_Code[2], ~Func_Code[0]);  // AND_Gate
  and and_13 (and_13_out, and_12_out, _000000);
  and and_14 (Sltu, Func_Code[0], and_26_out);
  and and_15 (Divu, Func_Code[0], and_25_out);
  and and_16 (and_16_out, Func_Code[5], ~Func_Code[4], Func_Code[3], ~Func_Code[2], Func_Code[1]);  // AND_Gate
  and and_17 (Slt, ~Func_Code[0], and_26_out);  // AND_Gate
  and and_18 (Xor, Func_Code[5], ~Func_Code[4], Func_Code[3], ~Func_Code[2], ~Func_Code[1], ~Func_Code[0], _000000);  // AND_Gate
  nand nand_1 (nand_1_out, Func_Code[5], Func_Code[4], Func_Code[3]);
  and and_19 (and_19_out, ~Func_Code[2], ~Func_Code[1], Func_Code[0]);  // AND_Gate
  and and_20 (and_20_out, Func_Code[2], ~Func_Code[1], ~Func_Code[0]);  // AND_Gate
  and and_21 (and_21_out, ~Func_Code[5], Func_Code[4], Func_Code[3], ~Func_Code[2], Func_Code[1]);  // AND_Gate
  and and_22 (Div, ~Func_Code[0], and_25_out);  // AND_Gate
  and and_23 (and_23_out, nand_1_out, _111111);
  and and_24 (and_24_out, ~Func_Code[2], Func_Code[1], ~Func_Code[0]);  // AND_Gate
  and and_25 (and_25_out, and_21_out, _000000);
  and and_26 (and_26_out, and_16_out, _000000);
  and and_27 (Tty, and_23_out, and_19_out);
  and and_28 (Rnd, and_23_out, and_24_out);
  and and_29 (Kbd, and_23_out, and_20_out);
  and and_30 (Sub, Func_Code[1], and_38_out);
  and and_31 (Or, Func_Code[0], and_37_out);
  and and_32 (And, ~Func_Code[0], and_37_out);  // AND_Gate
  and and_33 (Jr, ~Func_Code[5], ~Func_Code[4], Func_Code[3], ~Func_Code[2], ~Func_Code[1], ~Func_Code[0], _000000);  // AND_Gate
  and and_34 (Add, ~Func_Code[1], and_38_out);  // AND_Gate
  and and_35 (and_35_out, Func_Code[5], ~Func_Code[4], ~Func_Code[3], Func_Code[2], ~Func_Code[1]);  // AND_Gate
  and and_36 (and_36_out, Func_Code[5], ~Func_Code[4], ~Func_Code[3], ~Func_Code[2], ~Func_Code[0]);  // AND_Gate
  and and_37 (and_37_out, and_35_out, _000000);
  and and_38 (and_38_out, and_36_out, _000000);
  and and_39 (Halt, Func_Code[5], Func_Code[4], Func_Code[3], Func_Code[2], Func_Code[1], Func_Code[0], _111111);
endmodule

module Instruction_Decoder (
  input  [31:0] Instruction,
  output Nop,
  output Pop,
  output Push,
  output Add,
  output Slt,
  output Jr,
  output Sub,
  output Sltu,
  output Mfhi,
  output Mult,
  output And,
  output Mflo,
  output Mulu,
  output Or,
  output Halt,
  output Div,
  output Nor,
  output Tty,
  output Divu,
  output Xor,
  output Rnd,
  output Kbd,
  output Lw,
  output J,
  output Addi,
  output Sw,
  output Slti,
  output Beq,
  output Sltiu,
  output Bne,
  output Andi,
  output Blez,
  output Xori,
  output Bgtz,
  output Ori,
  output Bltz,
  output [5:0] Op_Code,
  output [4:0] Rs,
  output [4:0] Rt,
  output [4:0] Rd,
  output [25:0] Destino_Salto,
  output [4:0] X,
  output [15:0] Constante,
  output [5:0] Func_Code
);

  wire _000000, _111000, _111111;
  wire [5:0] not_1_out, not_2_out;

  assign not_1_out = ~Instruction[31:26];  // NOT_Gate not_1, 6 bits wide
  and and_1 (_000000, not_1_out[0], not_1_out[1], not_1_out[2], not_1_out[3], not_1_out[4], not_1_out[5]);
  and and_2 (_111111, Instruction[26], Instruction[27], Instruction[28], Instruction[29], Instruction[30], Instruction[31]);
  assign not_2_out = ~Instruction[31:26];  // NOT_Gate not_2, 6 bits wide
  and and_3 (J, not_2_out[0], ~not_2_out[1], not_2_out[2], not_2_out[3], not_2_out[4], not_2_out[5]);  // AND_Gate
  and and_4 (_111000, ~Instruction[26], ~Instruction[27], ~Instruction[28], Instruction[29], Instruction[30], Instruction[31]);  // AND_Gate
  TipoI tipoi_1 (
    .in_1(Instruction[31:26]), .Addi(Addi), .Xori(Xori), .Beq(Beq), .Bltz(Bltz), .Slti(Slti), .Ori(Ori),
    .Bne(Bne), .Sltiu(Sltiu), .Lw(Lw), .Blez(Blez), .Andi(Andi), .Sw(Sw), .Bgtz(Bgtz));
  Tipo_R tipo_r_1 (
    .Func_Code(Instruction[5:0]), ._000000(_000000), ._111000(_111000), ._111111(_111111), .Nop(Nop),
    .Mulu(Mulu), .Slt(Slt), .Nor(Nor), .Mfhi(Mfhi), .Add(Add), .Div(Div), .Sltu(Sltu), .Xor(Xor),
    .Mflo(Mflo), .Sub(Sub), .Divu(Divu), .And(And), .Push(Push), .Halt(Halt), .Mul(Mult), .Pop(Pop), .Or(Or),
    .Jr(Jr), .Tty(Tty), .Rnd(Rnd), .Kbd(Kbd));

  assign Constante = Instruction[15:0];
  assign Destino_Salto = Instruction[25:0];
  assign Func_Code = Instruction[5:0];
  assign Op_Code = Instruction[31:26];
  assign Rd = Instruction[15:11];
  assign Rs = Instruction[25:21];
  assign Rt = Instruction[20:16];
  assign X = Instruction[10:6];
endmodule

module Branch_Control (
  input  [25:0] Destino,
  input  [31:0] RT,
  input  [31:0] PC,
  input  [15:0] Offset,
  input  BEQ,
  input  JR,
  input  [31:0] RS,
  input  BNE,
  input  BLTZ,
  input  BLEZ,
  input  BGTZ,
  input  J,
  output [31:0] Output
);

  wire and_2_out, and_3_out, and_4_out, and_5_out, and_6_out, or_1_out, RS___0, RS___0_t, RS____0, RS____0_t,
       RS____RT, RS____RT_t;
  wire [1:0] Selector;
  wire [31:0] PC_4, PC_4_4_Offset;
  wire [31:18] _4_Offset;

  Comparator_part #(.width(32)) comparator_1 (.a(RS), .b(RT), .eq(RS____RT_t));  // open: gt, lt
  not not_1 (RS____RT, RS____RT_t);
  Comparator_part #(.width(32)) comparator_2 (.a(RS), .b({32{1'b0}}), .gt(RS___0_t), .eq(RS____0_t), .lt(RS___0));
  Multiplexer #(.select(2), .width(32), .enable("false")) multiplexer_1 (
    .in0(PC_4), .in1(PC_4_4_Offset), .in2({PC[31:28], Destino, 2'b00}), .in3(RS), .out(Output), .sel(Selector));
  and and_1 (RS____0, RS____0_t, RS___0);
  and and_2 (and_2_out, BEQ, RS____RT_t);
  and and_3 (and_3_out, BNE, RS____RT);
  and and_4 (and_4_out, BLTZ, RS___0);
  and and_5 (and_5_out, BGTZ, RS___0_t);
  and and_6 (and_6_out, BLEZ, RS____0);
  Adder #(.width(32)) adder_1 (.a(PC), .b(32'h4), .out(PC_4));  // open: cin, cout
  or or_1 (or_1_out, and_2_out, and_3_out, and_4_out, and_5_out, and_6_out);
  Adder #(.width(32)) adder_2 (.a(PC_4), .b({_4_Offset, Offset, 2'b00}), .out(PC_4_4_Offset));  // open: cin, cout
  Multiplexer #(.width(14), .enable("false")) multiplexer_2 (
    .in0({14{1'b0}}), .in1({14{1'b1}}), .out(_4_Offset), .sel(Offset[15]));
  or or_2 (Selector[0], or_1_out, JR);
  or or_3 (Selector[1], JR, J);

  // Other names for the same wires on the sheet: _4_Offset[17:2] = Offset; Jump[31:2] = {PC[31:28], Destino}
endmodule

module Memory_Address (
  input  Pop,
  input  [31:0] Alu,
  input  Push,
  input  Lw,
  input  Sw,
  input  [31:0] PC,
  input  EnPC,
  input  [31:0] SP,
  output [31:0] Output
);

  wire [1:0] or_1_out;
  wire [31:0] multiplexer_1_out, SP_4;

  Multiplexer #(.width(32), .enable("false")) multiplexer_1 (.in0(SP), .in1(SP_4), .out(multiplexer_1_out), .sel(Push));
  Subtractor #(.width(32)) subtractor_1 (.a(SP), .b(32'h4), .out(SP_4));  // open: bin, bout
  Multiplexer #(.select(2), .width(32), .enable("false")) multiplexer_2 (
    .in0(PC), .in1(Alu), .in2(multiplexer_1_out), .in3(PC), .out(Output), .sel(or_1_out));
  or or_1 (or_1_out[0], Lw, EnPC, Lw);
  or or_2 (or_1_out[1], Pop, EnPC, Push);
endmodule

module Ram_Reader (
  input  [3:0] Read_Time,
  input  [31:0] Bank_1,
  input  [31:0] Bank_3,
  input  Clk,
  input  Reset,
  input  Get,
  input  [31:0] Bank_2,
  input  [31:0] Bank_4,
  output CS,
  output [31:0] Bank_Out_1,
  output [31:0] Bank_Out_3,
  output Ready,
  output [31:0] Bank_Out_2,
  output [31:0] Bank_Out_4
);

  wire A, B, or_1_out, Stop;

  D_Flip_Flop #(.trigger("falling")) d_ff_1 (.clk(Clk), .D(Get), .Q(A), .en(or_1_out));  // open: Qn, preset, reset
  or or_1 (or_1_out, Get, Stop);
  Timer timer_1 (.Start(A), .Reset(Reset), .Time(Read_Time), .Clk(Clk), .Ready(Stop));
  D_Flip_Flop #(.trigger("falling")) d_ff_2 (.clk(Clk), .D(Stop), .Qn(B), .reset(Ready));  // open: Q, preset, en
  D_Flip_Flop #(.trigger("falling")) d_ff_3 (.clk(Clk), .D(B), .Q(Ready));  // open: Qn, preset, en, reset
  or or_2 (CS, A, B);
  Register #(.width(32)) register_1 (.D(Bank_1), .en(B), .Q(Bank_Out_1), .clk(Clk), .clr(Reset));
  Register #(.width(32)) register_2 (.D(Bank_2), .en(B), .Q(Bank_Out_2), .clk(Clk), .clr(Reset));
  Register #(.width(32)) register_3 (.D(Bank_3), .en(B), .Q(Bank_Out_3), .clk(Clk), .clr(Reset));
  Register #(.width(32)) register_4 (.D(Bank_4), .en(B), .Q(Bank_Out_4), .clk(Clk), .clr(Reset));
endmodule

module Ram_Interaction (
  input  Clk,
  input  Reset,
  input  [31:0] Bank_1,
  input  [31:0] Bank_3,
  input  [31:0] DP_Address,
  input  Write,
  input  Get_Inst,
  input  Get_Data,
  input  Is_Inst,
  input  [3:0] Read_Time,
  input  [31:0] Bank_2,
  input  [31:0] Bank_4,
  input  [3:0] Write_Time,
  output [15:0] ADDR,
  output [31:0] Bank_Output_1,
  output [31:0] Bank_Output_3,
  output [3:0] Mask,
  output RW,
  output CS,
  output [31:0] Bank_Output_2,
  output [31:0] Bank_Output_4,
  output Ready_Inst,
  output Ready_Data,
  output Ready_Write
);

  wire CS_1, CS_2, or_1_out, Stop;
  wire [31:0] A___Bank_Output_1, A___Bank_Output_2, A___Bank_Output_3, A___Bank_Output_4, B___Bank_Output_1,
       B___Bank_Output_2, B___Bank_Output_3, B___Bank_Output_4, inout_1_output, inout_2_output,
       inout_3_output, inout_4_output;

  InOut inout_1 (.in_1(B___Bank_Output_1), .Output(inout_1_output));
  InOut inout_2 (.in_1(B___Bank_Output_3), .Output(inout_2_output));
  Demultiplexer #(.select(2), .enable("false")) demultiplexer_1 (
    .out0(Mask[0]), .out1(Mask[1]), .out2(Mask[2]), .out3(Mask[3]), .in(1'b1), .sel(DP_Address[3:2]));
  Multiplexer #(.width(32), .enable("false")) multiplexer_1 (
    .in0(inout_1_output), .in1(A___Bank_Output_1), .out(Bank_Output_1), .sel(Is_Inst));
  Multiplexer #(.width(32), .enable("false")) multiplexer_2 (
    .in0(inout_2_output), .in1(A___Bank_Output_3), .out(Bank_Output_3), .sel(Is_Inst));
  Ram_Reader ram_reader_1 (
    .Read_Time(Read_Time), .Bank_1(Bank_1), .Bank_3(Bank_3), .Clk(Clk), .Reset(Reset), .Get(Get_Inst),
    .Bank_2(Bank_2), .Bank_4(Bank_4), .CS(CS_1), .Bank_Out_1(A___Bank_Output_1),
    .Bank_Out_3(A___Bank_Output_3), .Ready(Ready_Inst), .Bank_Out_2(A___Bank_Output_2),
    .Bank_Out_4(A___Bank_Output_4));
  or or_1 (or_1_out, Write, Stop);
  D_Flip_Flop #(.trigger("falling")) d_ff_1 (.clk(Clk), .D(Write), .Q(RW), .en(or_1_out));  // open: Qn, preset, reset
  InOut inout_3 (.in_1(B___Bank_Output_2), .Output(inout_3_output));
  InOut inout_4 (.in_1(B___Bank_Output_4), .Output(inout_4_output));
  Timer timer_1 (.Start(RW), .Reset(Ready_Write), .Time(Write_Time), .Clk(Clk), .Ready(Stop));
  Multiplexer #(.width(32), .enable("false")) multiplexer_3 (
    .in0(inout_3_output), .in1(A___Bank_Output_2), .out(Bank_Output_2), .sel(Is_Inst));
  Multiplexer #(.width(32), .enable("false")) multiplexer_4 (
    .in0(inout_4_output), .in1(A___Bank_Output_4), .out(Bank_Output_4), .sel(Is_Inst));
  Ram_Reader ram_reader_2 (
    .Read_Time(Read_Time), .Bank_1(Bank_1), .Bank_3(Bank_3), .Clk(Clk), .Reset(Reset), .Get(Get_Data),
    .Bank_2(Bank_2), .Bank_4(Bank_4), .CS(CS_2), .Bank_Out_1(B___Bank_Output_1),
    .Bank_Out_3(B___Bank_Output_3), .Ready(Ready_Data), .Bank_Out_2(B___Bank_Output_2),
    .Bank_Out_4(B___Bank_Output_4));
  D_Flip_Flop #(.trigger("falling")) d_ff_2 (.clk(Clk), .D(Stop), .Q(Ready_Write));  // open: Qn, preset, en, reset
  or or_2 (CS, CS_2, RW, CS_1);

  assign ADDR = DP_Address[19:4];
endmodule

module Control_Unit (
  input  Clk,
  input  Start,
  input  Ready_Inst,
  input  Alu_Inst,
  input  R_Inst,
  input  Reset,
  input  Tty_Inst,
  input  Ready_Data,
  input  Jmp_Inst,
  input  Mem_Inst,
  input  Write_Inst,
  input  Ready_W,
  output Use_RF,
  output End,
  output Get_Inst,
  output Tty_En,
  output Write,
  output Use_PC,
  output Get_Data,
  output Use_GI,
  output Kbd_En
);

  wire Branch, d_ff_1_q, d_ff_2_q, d_ff_3_q, d_ff_5_q, demultiplexer_1_out0, demultiplexer_1_out1, or_5_out,
       RF, Tty_t;
  wire [2:0] or_2_out;

  and and_1 (Tty_En, Tty_Inst, Tty_t);
  D_Flip_Flop #(.trigger("falling")) d_ff_1 (
    .clk(Clk), .D(Start), .Q(d_ff_1_q), .reset(Reset));  // open: Qn, preset, en
  D_Flip_Flop #(.trigger("falling")) d_ff_2 (
    .clk(Clk), .D(Use_PC), .Q(d_ff_2_q), .reset(Reset));  // open: Qn, preset, en
  or or_1 (Get_Inst, d_ff_1_q, d_ff_2_q);
  D_Flip_Flop #(.trigger("falling")) d_ff_3 (.clk(Clk), .D(Ready_Inst), .Q(d_ff_3_q));  // open: Qn, preset, en, reset
  Demultiplexer #(.select(3), .enable("false")) demultiplexer_1 (
    .out0(demultiplexer_1_out0), .out1(demultiplexer_1_out1), .out2(Branch), .out3(RF), .out4(Get_Data),
    .out5(Write), .in(d_ff_3_q), .sel(or_2_out));  // open: out6, out7
  or or_2 (or_2_out[0], R_Inst, Alu_Inst, Write_Inst);
  or or_3 (or_2_out[1], R_Inst, Jmp_Inst);
  or or_4 (or_2_out[2], Mem_Inst, Write_Inst);
  or or_5 (or_5_out, End, demultiplexer_1_out0);
  D_Flip_Flop #(.trigger("falling")) d_ff_4 (.clk(Clk), .D(or_5_out), .Q(End), .reset(Reset));  // open: Qn, preset, en
  D_Flip_Flop #(.trigger("falling")) d_ff_5 (
    .clk(Clk), .D(demultiplexer_1_out1), .Q(d_ff_5_q), .reset(Reset));  // open: Qn, preset, en
  or or_6 (Use_RF, d_ff_5_q, Ready_Data, RF);
  D_Flip_Flop #(.trigger("falling")) d_ff_6 (.clk(Clk), .D(Use_RF), .Q(Kbd_En));  // open: Qn, preset, en, reset
  or or_7 (Use_PC, Kbd_En, Ready_W, Branch);

  assign Use_GI = Ready_Inst;

  // Other names for the same wires on the sheet: Cont = Use_PC; Tty = Kbd_En
endmodule

module Data_Path (
  input  Clk,
  input  Reset,
  input  [31:0] Instruction,
  input  MemW,
  input  EnGI,
  input  EnPC,
  input  [6:0] kbd_data,
  input  EnRF,
  input  KbdAva,
  output Alu_Inst,
  output Halt,
  output [31:0] R_out,
  output Tty,
  output Mem_Inst,
  output Stack_Inst,
  output Jmp_Inst,
  output Write_Inst,
  output R_Inst,
  output [31:0] Address,
  output [6:0] Tty_Data
);

  wire Add, Addi, alu_encoder_1_unsigned, And, Andi, Beq, Bgtz, Blez, Bltz, Bne, Div, Divu, Inmediately, J,
       Jr, Kbd, Lw, Mfhi, Mflo, Mult, Mulu, Nop, Nor, ON, Or, or_1_out, Ori, Pop, Push, Rnd, Slt, Slti,
       Sltiu, Sltu, Sub, Sw, Xor, Xori;
  wire [2:0] RF_selector;
  wire [3:0] alu_encoder_1_opselect;
  wire [4:0] multiplexer_1_out, RD, Rd_t, RS, Rs_t, RT, Rt_t, X;
  wire [5:0] Func_Code, Op_Code;
  wire [15:0] Constante;
  wire [25:0] Destino_Salto;
  wire [31:0] ALU_Result, Alu_Result_t, branch_control_1_output, ExtKbd, get_instruction_1_output, HI,
       Input_RF, LO, PC, Random, RT__star, RT_t_t, SP, SP_t;
  wire [31:7] RS_t_t;
  wire [31:31] and_1_out;

  Get_Instruction get_instruction_1 (
    .Instruction(Instruction), .Enable(EnGI), .Reset(Reset), .Clk(Clk), .Output(get_instruction_1_output));
  or or_1 (or_1_out, Sw, Andi, Lw);
  and and_1 (and_1_out[31], Constante[0], ~Ori, ~Xori, ~Andi);  // AND_Gate
  Multiplexer #(.width(5), .enable("false")) multiplexer_1 (
    .in0(RD), .in1(RT), .out(multiplexer_1_out), .sel(Inmediately));
  Multiplexer #(.width(32), .enable("false")) multiplexer_2 (
    .in0(RT_t_t), .in1({{16{and_1_out[31]}}, Constante[0], Constante[15:1]}), .out(RT__star),
    .sel(Inmediately));
  Alu_Encoder alu_encoder_1 (
    .Add(Add), .Sub(Sub), .Mult(Mult), .Mulu(Mulu), .Div(Div), .Divu(Divu), .Slt(Slt), .Sltu(Sltu),
    .And(And), .Or(Or), .Nor(Nor), .Xor(Xor), .Addi(Addi), .Slti(Slti), .Sltiu(Sltiu), .Andi(or_1_out),
    .Xori(Xori), .Ori(Ori), .Output(ON), .OpSelect(alu_encoder_1_opselect),
    .Unsigned(alu_encoder_1_unsigned), .Inmediately(Inmediately));
  Timer timer_1 (.Reset(Push));  // open: Start, Time, Clk, Ready
  Instruction_Decoder instruction_decoder_1 (
    .Instruction(get_instruction_1_output), .Nop(Nop), .Pop(Pop), .Push(Push), .Add(Add), .Slt(Slt), .Jr(Jr),
    .Sub(Sub), .Sltu(Sltu), .Mfhi(Mfhi), .Mult(Mult), .And(And), .Mflo(Mflo), .Mulu(Mulu), .Or(Or),
    .Halt(Halt), .Div(Div), .Nor(Nor), .Tty(Tty), .Divu(Divu), .Xor(Xor), .Rnd(Rnd), .Kbd(Kbd), .Lw(Lw),
    .J(J), .Addi(Addi), .Sw(Sw), .Slti(Slti), .Beq(Beq), .Sltiu(Sltiu), .Bne(Bne), .Andi(Andi), .Blez(Blez),
    .Xori(Xori), .Bgtz(Bgtz), .Ori(Ori), .Bltz(Bltz), .Op_Code(Op_Code), .Rs(Rs_t), .Rt(Rt_t), .Rd(Rd_t),
    .Destino_Salto(Destino_Salto), .X(X), .Constante(Constante), .Func_Code(Func_Code));
  Register_File register_file_1 (
    .Reset(Reset), .Write(EnRF), .IN_A(RS), .Input(Input_RF), .Pop(Pop), .IN_B(RT), .MemRW(EnPC),
    .Push(Push), .SEL(multiplexer_1_out), .Output_A({RS_t_t, Tty_Data}), .Output_B(RT_t_t), .Output_SP(SP_t),
    .Clk(Clk));
  // ALU alu_1: pin names not known; wires that end beside it: {RS_t_t, Tty_Data}, RT__star, alu_encoder_1_opselect, ON, alu_encoder_1_unsigned, Clk, LO, ALU_Result, HI
  Multiplexer #(.select(3), .width(32), .enable("false")) multiplexer_3 (
    .in0(Alu_Result_t), .in1(Instruction), .in2(HI), .in3(LO), .in4(Random), .in5(ExtKbd), .out(Input_RF),
    .sel(RF_selector));  // open: in6, in7
  or or_2 (Write_Inst, Push, Sw);
  or or_3 (Stack_Inst, Pop, Push);
  or or_4 (Mem_Inst, Lw, Sw);
  assign ExtKbd = {{25{1'b0}}, kbd_data};  // Bit_Extender bit_extender_1
  Random #(.width(32)) random_1 (.clk(Clk), .next(Rnd), .out(Random));  // open: clr
  Memory_Address memory_address_1 (
    .Pop(Pop), .Alu(ALU_Result), .Push(Push), .Lw(Lw), .Sw(Sw), .PC(PC), .EnPC(MemW), .SP(SP),
    .Output(Address));
  or or_5 (RF_selector[0], Lw, Pop, Mflo, Kbd);
  or or_6 (RF_selector[1], Mflo, Mfhi);
  or or_7 (RF_selector[2], Rnd, Kbd);
  or or_8 (Alu_Inst, Andi, Div, Xori, Divu, Ori, And, Slti, Mult, Sltiu, Sub, Add, Addi, Mulu, Xor, Slt, Nor, Sltu, Or);
  or or_9 (Jmp_Inst, Jr, Nop, Beq, Blez, J, Bltz, Bne, Bgtz);
  Branch_Control branch_control_1 (
    .Destino(Destino_Salto), .RT(RT_t_t), .PC(PC), .Offset(Constante), .BEQ(Beq), .JR(Jr),
    .RS({RS_t_t, Tty_Data}), .BNE(Bne), .BLTZ(Bltz), .BLEZ(Blez), .BGTZ(Bgtz), .J(J),
    .Output(branch_control_1_output));
  or or_10 (R_Inst, Mflo, Kbd, Rnd, Tty, Mfhi);
  PC pc_1 (.Input(branch_control_1_output), .Enable(EnPC), .Output(PC), .Clk(Clk), .Reset(Reset));
  Multiplexer #(.width(32), .enable("false")) multiplexer_4 (
    .in0({RS_t_t, Tty_Data}), .in1(RT_t_t), .out(R_out), .sel(Sw));

  // Other names for the same wires on the sheet: RS_t_t[6:0] = Tty_Data
endmodule
